# Fritzing sketch MidiController (saved by Fritzing 0.9.3b)
breadboards: 1

parts:
  Componente1 = Arduino Uno (Rev3)
  LED2 = LED - 5mm [color="Green (555nm)" package="5 mm [THT]"]
  LED3 = LED - 5mm [color="Red (633nm)" package="5 mm [THT]"]
  R3 = Resistor [tolerance=±5% resistance=220 package=THT]
  R4 = Resistor [tolerance=±5% resistance=220 package=THT]
  LED4 = LED - 5mm [color="Green (555nm)" package="5 mm [THT]"]
  S1 = Pushbutton [package=THT]
  S2 = Pushbutton [package=THT]
  S3 = Pushbutton [package="[THT]"]
  R2 = Resistor [tolerance=±5% resistance=220 package=THT]
  S4 = Pushbutton [package="[THT]"]
  S5 = Pushbutton [package="[THT]"]
  S6 = Pushbutton [package="[THT]"]
  S7 = Pushbutton [package="[THT]"]

nets:
  N1: Componente1.D8, S3.Pin_3, S3.Pin_4
  N2: Componente1.D10_PWM/SS, R3.Pin_1
  N3: Componente1.D11_PWM/MOSI, R4.Pin_1
  N4: Componente1.D12/MISO, R2.Pin_1
  N5: Componente1.GND, LED2.cathode, S1.leg0, S2.leg0, S3.Pin_1, S3.Pin_2, S4.Pin_1, S4.Pin_2, S5.Pin_1, S5.Pin_2, S6.Pin_1, S6.Pin_2, S7.Pin_1, S7.Pin_2
  N6: Componente1.D2, S2.leg1
  N7: Componente1.D3_PWM, S1.leg1
  N8: Componente1.D4, S7.Pin_3, S7.Pin_4
  N9: Componente1.D5_PWM, S6.Pin_3, S6.Pin_4
  N10: Componente1.D6_PWM, S5.Pin_3, S5.Pin_4
  N11: Componente1.D7, S4.Pin_3, S4.Pin_4
  N12: LED2.anode, R2.Pin_0
  N13: LED3.anode, R3.Pin_0
  N14: R4.Pin_0, LED4.anode
